// Logisim project my_own_computer.circ as structural Verilog
module my_computer (
  input  in_1,
  input  [15:0] in_2,
  input  in_3,
  input  in_4,
  input  in_5,
  output [15:0] out_6
);

  wire clock_1_out, e_ACC, e_CONST, e_D, e_IAR, e_JR, e_R0, e_R1, e_R2, e_ROM, my_control_unit_1_step_0,
       my_control_unit_1_step_1, my_control_unit_1_step_2, my_control_unit_1_step_3,
       my_control_unit_1_step_4, my_control_unit_1_step_5, my_control_unit_1_step_6,
       my_control_unit_1_step_7, my_control_unit_1_step_8, my_control_unit_1_step_8_2,
       my_control_unit_1_step_9, my_control_unit_1_step_10, my_control_unit_1_step_11,
       my_control_unit_1_step_12, s_ACC, s_D, s_IAR, s_IR, s_JR, s_PCAR, s_R0, s_R1, s_R2, s_TMP;
  wire [3:0] op_code;
  wire [15:0] ACC_info, ALU_o, D_info, IR_o, MAR_o, PCAR_o, R0_info, R1_info, R2_info, ram_1_dout,
       rom_1_data, TMP_o;

  Clock clock_1 (.out(clock_1_out));
  assign out_6 = in_1 ? in_2 : 16'bz;  // Controlled_Buffer controlled_buffer_1
  my_control_unit my_control_unit_1 (
    .clk(clock_1_out), .instr(IR_o), .e_D(e_D), .s_D(s_D), .e_JR(e_JR), .s_JR(s_JR), .e_R0(e_R0),
    .s_R0(s_R0), .e_R1(e_R1), .s_R1(s_R1), .e_R2(e_R2), .s_R2(s_R2), .s_IR(s_IR), .e_ACC(e_ACC),
    .s_ACC(s_ACC), .s_TMP(s_TMP), .s_PCAR(s_PCAR), .e_ROM(e_ROM), .e_CONST(e_CONST), .e_IAR(e_IAR),
    .s_IAR(s_IAR), .op_code(op_code), .step_0(my_control_unit_1_step_0), .step_1(my_control_unit_1_step_1),
    .step_2(my_control_unit_1_step_2), .step_3(my_control_unit_1_step_3), .step_4(my_control_unit_1_step_4),
    .step_5(my_control_unit_1_step_5), .step_6(my_control_unit_1_step_6), .step_7(my_control_unit_1_step_7),
    .step_8(my_control_unit_1_step_8), .step_8_2(my_control_unit_1_step_8_2),
    .step_9(my_control_unit_1_step_9), .step_10(my_control_unit_1_step_10),
    .step_11(my_control_unit_1_step_11), .step_12(my_control_unit_1_step_12));  // open: e_IR, s_MAR, s_RAM, e_RAM
  assign out_6 = e_CONST ? 16'h1 : 16'bz;  // Controlled_Buffer controlled_buffer_2
  my_reg IAR (.i(out_6), .s(s_IAR), .e(e_IAR), .o(out_6));  // open: info
  my_reg D (.i(out_6), .s(s_D), .e(e_D), .o(out_6), .info(D_info));
  my_reg JR (.i(out_6), .o(out_6));  // open: s, e, info
  my_reg R0 (.i(out_6), .s(s_R0), .e(e_R0), .o(out_6), .info(R0_info));
  // Probe on R0_info
  my_reg R1 (.i(out_6), .s(s_R1), .e(e_R1), .o(out_6), .info(R1_info));
  // Probe on R1_info
  my_reg R2 (.i(out_6), .s(s_R2), .e(e_R2), .o(out_6), .info(R2_info));
  // Probe on R2_info
  my_reg IR (.i(out_6), .s(s_IR), .e(1'b1), .o(IR_o));  // open: info
  // Probe on D_info
  // Probe on out_6
  Controlled_Buffer #(.width(16)) controlled_buffer_3 (.in(IR_o), .out(out_6));  // open: en
  LED led_1 (.in(my_control_unit_1_step_0));
  LED led_2 (.in(my_control_unit_1_step_1));
  LED led_3 (.in(my_control_unit_1_step_2));
  LED led_4 (.in(my_control_unit_1_step_3));
  LED led_5 (.in(my_control_unit_1_step_4));
  LED led_6 (.in(my_control_unit_1_step_5));
  LED led_7 (.in(my_control_unit_1_step_6));
  LED led_8 (.in(my_control_unit_1_step_7));
  LED led_9 (.in(my_control_unit_1_step_8));
  LED led_10 (.in(my_control_unit_1_step_8_2));
  LED led_11 (.in(my_control_unit_1_step_9));
  LED led_12 (.in(my_control_unit_1_step_10));
  LED led_13 (.in(my_control_unit_1_step_11));
  LED led_14 (.in(my_control_unit_1_step_12));
  RAM #(.addrWidth(16), .dataWidth(16), .trigger("high")) ram_1 (
    .addr(MAR_o), .we(in_4), .oe(1'b1), .din(out_6), .dout(ram_1_dout));
  ROM #(.addrWidth(16), .dataWidth(16)) rom_1 (.addr(PCAR_o), .data(rom_1_data));
  assign out_6 = in_5 ? ram_1_dout : 16'bz;  // Controlled_Buffer controlled_buffer_4
  assign out_6 = e_ROM ? rom_1_data : 16'bz;  // Controlled_Buffer controlled_buffer_5
  my_reg MAR (.i(out_6), .s(in_3), .e(1'b1), .o(MAR_o));  // open: info
  my_reg PCAR (.i(out_6), .s(s_PCAR), .e(1'b1), .o(PCAR_o));  // open: info
  my_reg TMP (.i(out_6), .s(s_TMP), .e(1'b1), .o(TMP_o));  // open: info
  my_reg ACC (.i(ALU_o), .s(s_ACC), .e(e_ACC), .o(out_6), .info(ACC_info));
  // Probe on ACC_info
  my_alu ALU (.a(TMP_o), .b(out_6), .op_code(op_code), .o(ALU_o));
  // Probe on ALU_o

  // Notes on the sheet:
  //   contents of rom_1 (hex, n*v repeats v):
  //   0 1 80 3000 4*6000
endmodule

module my_reg (
  input  [15:0] i,
  input  s,
  input  e,
  output [15:0] o,
  output [15:0] info
);

  Register #(.trigger("high"), .width(16)) register_1 (.D(i), .en(1'b1), .clk(s), .Q(info));  // open: clr
  assign o = e ? info : 16'bz;  // Controlled_Buffer controlled_buffer_1
endmodule

module my_alu (
  input  [15:0] a,
  input  [15:0] b,
  input  [3:0] op_code,
  output [15:0] o
);

  wire op_0, op_1, op_2, op_3, op_4, op_5, op_6, op_7, op_8;
  wire [15:0] adder_1_out, and_1_out, my_shift_left_1_o, my_shift_right_1_o, not_1_out, or_1_out,
       subtractor_1_out;

  Demultiplexer #(.select(4)) demultiplexer_1 (
    .out0(op_0), .out1(op_1), .out2(op_2), .out3(op_3), .out4(op_4), .out5(op_5), .out6(op_6), .out7(op_7),
    .out8(op_8), .in(1'b1), .sel(op_code));  // open: out9, out10, out11, out12, out13, out14, out15
  Adder #(.width(16)) adder_1 (.a(a), .b(b), .out(adder_1_out), .cin(1'b0));  // open: cout
  Subtractor #(.width(16)) subtractor_1 (.a(a), .b(b), .out(subtractor_1_out), .bin(1'b0));  // open: bout
  assign not_1_out = ~a;  // NOT_Gate not_1, 16 bits wide
  assign and_1_out = a & b;  // AND_Gate and_1, 16 bits wide
  assign or_1_out = a | b;  // OR_Gate or_1, 16 bits wide
  assign o = op_1 ? adder_1_out : 16'bz;  // Controlled_Buffer controlled_buffer_1
  assign o = op_2 ? subtractor_1_out : 16'bz;  // Controlled_Buffer controlled_buffer_2
  assign o = op_3 ? not_1_out : 16'bz;  // Controlled_Buffer controlled_buffer_3
  assign o = op_4 ? and_1_out : 16'bz;  // Controlled_Buffer controlled_buffer_4
  assign o = op_5 ? or_1_out : 16'bz;  // Controlled_Buffer controlled_buffer_5
  my_shift_left my_shift_left_1 (.i(a), .o(my_shift_left_1_o));  // open: sh_i, sh_o
  my_shift_right my_shift_right_1 (.i(a), .o(my_shift_right_1_o));  // open: sh_i, sh_o
  assign o = op_6 ? my_shift_left_1_o : 16'bz;  // Controlled_Buffer controlled_buffer_6
  assign o = op_7 ? my_shift_right_1_o : 16'bz;  // Controlled_Buffer controlled_buffer_7
endmodule

module my_shift_left (
  input  sh_i,
  input  [15:0] i,
  output [15:0] o,
  output sh_o
);


  assign o = {i[14:0], sh_i};
  assign sh_o = i[15];
endmodule

module my_shift_right (
  input  [15:0] i,
  input  sh_i,
  output sh_o,
  output [15:0] o
);


  assign o = {sh_i, i[15:1]};
  assign sh_o = i[0];
endmodule

module my_control_unit (
  input  clk,
  input  [15:0] instr,
  output e_D,
  output s_D,
  output e_JR,
  output s_JR,
  output e_R0,
  output s_R0,
  output e_R1,
  output s_R1,
  output e_R2,
  output s_R2,
  output e_IR,
  output s_IR,
  output e_ACC,
  output s_ACC,
  output s_TMP,
  output s_MAR,
  output s_RAM,
  output e_RAM,
  output s_PCAR,
  output e_ROM,
  output e_CONST,
  output e_IAR,
  output s_IAR,
  output [3:0] op_code,
  output step_0,
  output step_1,
  output step_2,
  output step_3,
  output step_4,
  output step_5,
  output step_6,
  output step_7,
  output step_8,
  output step_8_2,
  output step_9,
  output step_10,
  output step_11,
  output step_12
);

  wire add_instr, and_instr, clk_next_step, data_instr, demultiplexer_2_out0, demultiplexer_2_out1,
       demultiplexer_2_out2, demultiplexer_2_out8, demultiplexer_2_out9, demultiplexer_3_out0,
       demultiplexer_3_out1, demultiplexer_3_out2, demultiplexer_3_out8, demultiplexer_3_out9,
       demultiplexer_4_out0, demultiplexer_4_out1, demultiplexer_4_out2, demultiplexer_4_out8,
       demultiplexer_4_out9, demultiplexer_4_out10, demultiplexer_5_out0, demultiplexer_5_out1,
       demultiplexer_5_out2, demultiplexer_5_out8, demultiplexer_5_out9, demultiplexer_5_out10, e_ACC_step_4,
       e_ACC_step_4_ML1, e_ACC_step_4_ML2, e_ACC_step_12, e_CONST_step_3, e_CONST_step_11, e_D_A, e_D_B,
       e_IAR_step_0, e_IAR_step_2, e_IAR_step_5, e_IAR_step_10, e_JR_A, e_JR_B, e_R0_A, e_R0_B, e_R1_A,
       e_R1_B, e_R2_A, e_R2_B, e_R_A, e_R_A_step_2_ML1, e_R_A_step_2_ML2, e_R_A_step_2_move, e_R_B,
       e_R_B_step_3_ML2, e_ROM_step_1, e_ROM_step_6, enable, math_logic_one_reg, math_logic_two_regs,
       move_instr, not_1_out, not_2_out, not_3_out, not_4_out, not_5_out, not_6_out, not_7_out, not_9_out,
       not_10_out, not_11_out, not_12_out, not_13_out, not_14_out, not_15_out, not_16_out, not_17_out,
       not_18_out, not_19_out, not_20_out, not_21_out, not_22_out, not_instr, or_4_out, or_5_out, or_8_out,
       or_9_out, or_instr, s_ACC_step_3, s_ACC_step_3_ML1, s_ACC_step_3_ML2, s_ACC_step_11, s_D_A, s_D_B,
       s_D_step_6, s_IAR_step_4, s_IAR_step_12, s_IR_step_1, s_JR_A, s_JR_B, s_MAR_A, s_PCAR_step_0,
       s_PCAR_step_5, s_R0_A, s_R0_B, s_R1_A, s_R1_B, s_R2_A, s_R2_B, s_R_A, s_R_A_step_4_ML1, s_R_B,
       s_R_B_step_2_move, s_R_B_step_4_ML2, s_TMP_step_2, s_TMP_step_2_ML1, s_TMP_step_2_ML2, s_TMP_step_10,
       set, shl_instr, shr_instr, sub_instr;
  wire [3:0] counter_1_q;

  Counter #(.max('hf), .width(4)) counter_1 (
    .Q(counter_1_q), .clk(clk_next_step));  // open: load, D, count, carry, up, clr
  Demultiplexer #(.select(4)) demultiplexer_1 (
    .out0(step_0), .out1(step_1), .out2(step_2), .out3(step_3), .out4(step_4), .out5(step_5), .out6(step_6),
    .out7(step_7), .out8(step_8), .out9(step_8_2), .out10(step_9), .out11(step_10), .out12(step_11),
    .out13(step_12), .in(1'b1), .sel(counter_1_q));  // open: out14, out15
  and and_1 (e_IAR_step_10, enable, step_10);
  my_clock my_clock_1 (.clk(clk), .clk_next_step(clk_next_step), .clk_e(enable), .clk_s(set));
  or or_1 (s_D, s_D_step_6, s_D_A, s_D_B);
  or or_2 (e_D, e_D_B, e_D_A);
  or or_3 (s_ACC, s_ACC_step_3, s_ACC_step_11, s_ACC_step_3_ML2, s_ACC_step_3_ML1);
  or or_4 (or_4_out, instr[0], instr[1], instr[2], instr[3], instr[4], instr[5], instr[6], instr[7], instr[8], instr[9], instr[10], instr[11], instr[12], instr[13], instr[14], instr[15]);
  Multiplexer #(.width(4)) multiplexer_1 (.in0(instr[15:12]), .in1(4'b0001), .out(op_code), .sel(or_5_out));
  or or_5 (or_5_out, data_instr, step_11);
  not not_1 (not_1_out, instr[12]);
  not not_2 (not_2_out, instr[13]);
  not not_3 (not_3_out, instr[14]);
  not not_4 (not_4_out, instr[15]);
  not not_5 (not_5_out, instr[13]);
  not not_6 (not_6_out, instr[14]);
  not not_7 (not_7_out, instr[15]);
  or or_6 (e_ACC, e_ACC_step_4, e_ACC_step_12, e_ACC_step_4_ML2, e_ACC_step_4_ML1);
  or or_7 (e_ROM, e_ROM_step_1, e_ROM_step_6);
  not not_8 (data_instr, or_4_out);
  or or_8 (or_8_out, move_instr, add_instr, sub_instr, and_instr, or_instr);
  or or_9 (or_9_out, not_instr, shl_instr, shr_instr);
  not not_9 (not_9_out, data_instr);
  and and_2 (move_instr, not_1_out, not_2_out, not_3_out, not_4_out, not_9_out);
  and and_3 (add_instr, instr[12], not_5_out, not_6_out, not_7_out);
  and and_4 (e_IAR_step_0, enable, step_0);
  and and_5 (e_IAR_step_2, enable, data_instr, step_2);
  and and_6 (e_R_A_step_2_move, enable, step_2, move_instr);
  and and_7 (e_R_A_step_2_ML2, enable, step_2, math_logic_two_regs);
  and and_8 (e_R_A_step_2_ML1, enable, step_2, math_logic_one_reg);
  and and_9 (s_TMP_step_10, set, step_10);
  or or_10 (s_JR, s_JR_B, s_JR_A);
  or or_11 (e_JR, e_JR_B, e_JR_A);
  or or_12 (e_CONST, e_CONST_step_3, e_CONST_step_11);
  and and_10 (e_ACC_step_4, enable, step_4, data_instr);
  and and_11 (e_ACC_step_4_ML2, enable, step_4, math_logic_two_regs);
  and and_12 (e_ACC_step_4_ML1, enable, step_4, math_logic_one_reg);
  or or_13 (math_logic_two_regs, add_instr, sub_instr, and_instr, or_instr);
  or or_14 (math_logic_one_reg, not_instr, shl_instr, shr_instr);
  or or_15 (s_TMP, s_TMP_step_2, s_TMP_step_10, s_TMP_step_2_ML2, s_TMP_step_2_ML1);
  and and_13 (s_PCAR_step_0, set, step_0);
  and and_14 (s_TMP_step_2, set, data_instr, step_2);
  and and_15 (s_R_B_step_2_move, set, step_2, move_instr);
  and and_16 (s_TMP_step_2_ML2, set, step_2, math_logic_two_regs);
  and and_17 (s_TMP_step_2_ML1, set, step_2, math_logic_one_reg);
  not not_10 (not_10_out, instr[12]);
  not not_11 (not_11_out, instr[14]);
  not not_12 (not_12_out, instr[15]);
  not not_13 (not_13_out, instr[14]);
  not not_14 (not_14_out, instr[15]);
  and and_18 (e_CONST_step_11, enable, step_11);
  or or_16 (e_R0, e_R0_A, e_R0_B);
  or or_17 (s_R0, s_R0_A, s_R0_B);
  and and_19 (s_IAR_step_4, set, step_4, data_instr);
  and and_20 (s_R_B_step_4_ML2, set, step_4, math_logic_two_regs);
  and and_21 (s_R_A_step_4_ML1, set, step_4, math_logic_one_reg);
  and and_22 (sub_instr, not_10_out, instr[13], not_11_out, not_12_out);
  and and_23 (not_instr, instr[12], instr[13], not_13_out, not_14_out);
  or or_18 (e_IAR, e_IAR_step_0, e_IAR_step_2, e_IAR_step_5, e_IAR_step_10);
  or or_19 (s_IAR, s_IAR_step_4, s_IAR_step_12);
  and and_24 (e_ROM_step_1, enable, step_1);
  or or_20 (e_R1, e_R1_A, e_R1_B);
  or or_21 (s_R1, s_R1_A, s_R1_B);
  and and_25 (e_CONST_step_3, enable, data_instr, step_3);
  and and_26 (e_R_B_step_3_ML2, enable, step_3, math_logic_two_regs);
  and and_27 (e_IAR_step_5, enable, step_5, data_instr);
  and and_28 (s_ACC_step_11, set, step_11);
  not not_15 (not_15_out, instr[12]);
  not not_16 (not_16_out, instr[13]);
  not not_17 (not_17_out, instr[13]);
  not not_18 (not_18_out, instr[15]);
  not not_19 (not_19_out, instr[15]);
  or or_22 (e_R2, e_R2_A, e_R2_B);
  or or_23 (s_R2, s_R2_A, s_R2_B);
  and and_29 (s_IR_step_1, set, step_1);
  and and_30 (and_instr, not_15_out, not_16_out, instr[14], not_18_out);
  and and_31 (or_instr, instr[12], not_17_out, instr[14], not_19_out);
  and and_32 (s_ACC_step_3, set, data_instr, step_3);
  and and_33 (s_ACC_step_3_ML2, set, step_3, math_logic_two_regs);
  and and_34 (s_ACC_step_3_ML1, set, step_3, math_logic_one_reg);
  and and_35 (s_PCAR_step_5, set, step_5, data_instr);
  and and_36 (e_ACC_step_12, enable, step_12);
  buf or_24 (s_IR, s_IR_step_1);  // OR_Gate
  or or_25 (s_PCAR, s_PCAR_step_0, s_PCAR_step_5);
  and and_37 (e_ROM_step_6, enable, step_6, data_instr);
  and and_38 (s_IAR_step_12, set, step_12);
  not not_20 (not_20_out, instr[12]);
  not not_21 (not_21_out, instr[15]);
  not not_22 (not_22_out, instr[15]);
  and and_39 (shl_instr, not_20_out, instr[13], instr[14], not_21_out);
  and and_40 (shr_instr, instr[12], instr[13], instr[14], not_22_out);
  and and_41 (s_D_step_6, set, step_6, data_instr);
  buf or_26 (s_R_A, s_R_A_step_4_ML1);  // OR_Gate
  or or_27 (e_R_A, e_R_A_step_2_move, e_R_A_step_2_ML2, e_R_A_step_2_ML1);
  and and_42 (e_R0_A, demultiplexer_2_out0, e_R_A, enable);
  and and_43 (e_R1_A, demultiplexer_2_out1, e_R_A, enable);
  and and_44 (e_R2_A, demultiplexer_2_out2, e_R_A, enable);
  and and_45 (e_D_A, demultiplexer_2_out8, e_R_A, enable);
  and and_46 (e_JR_A, demultiplexer_2_out9, e_R_A, enable);
  and and_47 (e_R0_B, demultiplexer_3_out0, e_R_B, enable);
  and and_48 (e_R1_B, demultiplexer_3_out1, e_R_B, enable);
  and and_49 (e_R2_B, demultiplexer_3_out2, e_R_B, enable);
  and and_50 (e_D_B, demultiplexer_3_out8, e_R_B, enable);
  and and_51 (e_JR_B, demultiplexer_3_out9, e_R_B, enable);
  or or_28 (s_R_B, s_R_B_step_2_move, s_R_B_step_4_ML2);
  buf or_29 (e_R_B, e_R_B_step_3_ML2);  // OR_Gate
  Demultiplexer #(.select(4)) demultiplexer_2 (
    .out0(demultiplexer_2_out0), .out1(demultiplexer_2_out1), .out2(demultiplexer_2_out2),
    .out8(demultiplexer_2_out8), .out9(demultiplexer_2_out9), .in(1'b1), .sel(instr[7:4]));  // open: out3, out4, out5, out6, out7, out10, out11, out12, out13, out14, out15
  Demultiplexer #(.select(4)) demultiplexer_3 (
    .out0(demultiplexer_3_out0), .out1(demultiplexer_3_out1), .out2(demultiplexer_3_out2),
    .out8(demultiplexer_3_out8), .out9(demultiplexer_3_out9), .in(1'b1), .sel(instr[3:0]));  // open: out3, out4, out5, out6, out7, out10, out11, out12, out13, out14, out15
  Demultiplexer #(.select(4)) demultiplexer_4 (
    .out0(demultiplexer_4_out0), .out1(demultiplexer_4_out1), .out2(demultiplexer_4_out2),
    .out8(demultiplexer_4_out8), .out9(demultiplexer_4_out9), .out10(demultiplexer_4_out10), .in(1'b1),
    .sel(instr[7:4]));  // open: out3, out4, out5, out6, out7, out11, out12, out13, out14, out15
  Demultiplexer #(.select(4)) demultiplexer_5 (
    .out0(demultiplexer_5_out0), .out1(demultiplexer_5_out1), .out2(demultiplexer_5_out2),
    .out8(demultiplexer_5_out8), .out9(demultiplexer_5_out9), .out10(demultiplexer_5_out10), .in(1'b1),
    .sel(instr[3:0]));  // open: out3, out4, out5, out6, out7, out11, out12, out13, out14, out15
  and and_52 (s_R0_B, demultiplexer_5_out0, s_R_B, set);
  and and_53 (s_R1_B, demultiplexer_5_out1, s_R_B, set);
  and and_54 (s_R2_B, demultiplexer_5_out2, s_R_B, set);
  and and_55 (s_D_B, demultiplexer_5_out8, s_R_B, set);
  and and_56 (s_JR_B, demultiplexer_5_out9, s_R_B, set);
  and and_57 (s_MAR, demultiplexer_5_out10, s_R_B, set);
  and and_58 (s_R0_A, demultiplexer_4_out0, s_R_A, set);
  and and_59 (s_R1_A, demultiplexer_4_out1, s_R_A, set);
  and and_60 (s_R2_A, demultiplexer_4_out2, s_R_A, set);
  and and_61 (s_D_A, demultiplexer_4_out8, s_R_A, set);
  and and_62 (s_JR_A, demultiplexer_4_out9, s_R_A, set);
  and and_63 (s_MAR_A, demultiplexer_4_out10, s_R_A, set);

  // Other names for the same wires on the sheet: R_A_wires[3:0] = instr[7:4]; R_B_wires[3:0] = instr[3:0];
  //   s_MAR_B = s_MAR

  // Notes on the sheet:
  //   инструкции которые оперируют двумя регистрами
  //   инструкции которые оперируют только одним регистром
  //   D
  //   ACC
  //   ROM
  //   тут уже идет операция (считывание инструкции)
  //   увеличиваем IAR (счетски команд) на один
  //   JR
  //   TMP
  //   CONST
  //   R0
  //   вытаскиваем инструкцию
  //   если у нас дата инструкция то тогда мы должны вытащить следущюю ячейку памяти которая содержит константное значение
  //   MAR
  //   IAR
  //   R1
  //   RAM
  //   R2
  //   IR
  //   PCAR
  //   R_A
  //   R_B
endmodule

module my_clock (
  input  clk,
  output clk_next_step,
  output clk_e,
  output clk_s
);

  wire d_ff_1_q, not_1_out, not_2_out;

  not not_1 (not_1_out, clk);
  D_Flip_Flop #(.trigger("high")) d_ff_1 (.D(clk_e), .clk(not_1_out), .Q(d_ff_1_q));  // open: Qn, preset, reset
  not not_2 (not_2_out, d_ff_1_q);
  D_Flip_Flop #(.trigger("high")) d_ff_2 (.D(not_2_out), .clk(clk), .Q(clk_e));  // open: Qn, preset, reset
  not not_3 (clk_next_step, clk_e);
  and and_1 (clk_s, clk_e, clk);
  // Digital_Oscilloscope digital_oscilloscope_1: pin names not known; wires that end beside it: clk, clk_e, clk_s, clk_next_step
endmodule
